// Logisim project TN1.circ as structural Verilog: 4 circuits, main circuit FA
module FA (
  input  A,
  input  B,
  input  Cin,
  output S,
  output Cout
);

  wire and_1_out, and_2_out, xor_1_out;

  xor xor_1 (xor_1_out, A, B);
  and and_1 (and_1_out, B, A);
  xor xor_2 (S, xor_1_out, Cin);
  and and_2 (and_2_out, xor_1_out, Cin);
  or or_1 (Cout, and_1_out, and_2_out);
endmodule

module ADDSUB4 (
  input  [3:0] A,
  input  SUB,
  input  [3:0] B,
  output [3:0] S,
  output C
);

  wire fa_1_cout, fa_2_cout, fa_3_cout, xor_1_out, xor_2_out, xor_3_out, xor_4_out;

  xor xor_1 (xor_1_out, SUB, B[0]);
  xor xor_2 (xor_2_out, SUB, B[1]);
  xor xor_3 (xor_3_out, SUB, B[2]);
  xor xor_4 (xor_4_out, SUB, B[3]);
  FA fa_1 (.A(A[0]), .B(xor_1_out), .Cin(SUB), .S(S[0]), .Cout(fa_1_cout));
  FA fa_2 (.A(A[1]), .B(xor_2_out), .Cin(fa_1_cout), .S(S[1]), .Cout(fa_2_cout));
  FA fa_3 (.A(A[2]), .B(xor_3_out), .Cin(fa_2_cout), .S(S[2]), .Cout(fa_3_cout));
  FA fa_4 (.A(A[3]), .B(xor_4_out), .Cin(fa_3_cout), .S(S[3]), .Cout(C));
endmodule

module LT (
  input  A7,
  input  B7,
  input  R7,
  output LT
);

  wire and_1_out, and_2_out, and_3_out, not_1_out;

  not not_1 (not_1_out, B7);
  and and_1 (and_1_out, A7, not_1_out);
  and and_2 (and_2_out, A7, R7);
  and and_3 (and_3_out, not_1_out, R7);
  or or_1 (LT, and_1_out, and_2_out, and_3_out);
endmodule

module ALU8 (
  input  [7:0] A,
  input  [7:0] B,
  input  [2:0] OP,
  output [7:0] R,
  output Z,
  output LT_out
);

  wire [7:0] adder_1_out, adder_2_out, and_1_out, multiplexer_1_out, multiplexer_2_out, not_1_out, or_1_out,
       subtractor_1_out, subtractor_2_out, xor_1_out;

  assign and_1_out = A & B;  // AND_Gate and_1, 8 bits wide
  assign or_1_out = A | B;  // OR_Gate or_1, 8 bits wide
  assign not_1_out = ~A;  // NOT_Gate not_1, 8 bits wide
  assign xor_1_out = A ^ B;  // XOR_Gate xor_1, 8 bits wide
  Adder adder_1 (.a(A), .b(B), .out(adder_1_out));  // open: cin, cout
  Adder adder_2 (.a(A), .b(8'h1), .out(adder_2_out));  // open: cin, cout
  Subtractor subtractor_1 (.a(A), .b(8'h1), .out(subtractor_1_out));  // open: bin, bout
  Subtractor subtractor_2 (.a(A), .b(B), .out(subtractor_2_out));  // open: bin, bout
  Multiplexer #(.select(2), .width(8), .enable("false")) multiplexer_1 (
    .in0(adder_1_out), .in1(adder_2_out), .in2(subtractor_2_out), .in3(subtractor_1_out),
    .out(multiplexer_1_out), .sel(OP[1:0]));
  Multiplexer #(.select(2), .width(8), .enable("false")) multiplexer_2 (
    .in0(and_1_out), .in1(or_1_out), .in2(not_1_out), .in3(xor_1_out), .out(multiplexer_2_out), .sel(OP[1:0]));
  Multiplexer #(.width(8), .enable("false")) multiplexer_3 (
    .in0(multiplexer_1_out), .in1(multiplexer_2_out), .out(R), .sel(OP[2]));
  LT lt_1 (.A7(A[7]), .B7(B[7]), .R7(R[7]), .LT(LT_out));
  nor nor_1 (Z, R[0], R[1], R[2], R[3], R[4], R[5], R[6], R[7]);
endmodule
